# Fritzing sketch Artnet DMX Converter (saved by Fritzing 1.0.4)
circuit board: 9cm x 8cm
perfboards: 1

parts:
  U1 = LuaNode32 / ESP32 [part_number=ESP32S-PIN30]
  XLR1 = XLR NC3MAAH [package=nc3maah]
  XLR2 = XLR NC3MAAH [package=nc3maah]
  C1_220uF = Capacitor Polarized [package=panasonic_e]
  C2_100nF = Capacitor [package=cap-pth-5mm]
  C3_100nF = Capacitor [package=cap-pth-5mm]
  C4_100nF = Capacitor [package=cap-pth-5mm]
  X1 = USB Connectors [package=usb-microb]
  Squix1 = OLED 0.96" 128x64 I2C SSD1306
  M1 = MAX485 Breakout [package=THT]
  M2 = MAX485 Breakout [package=THT]
  C2_100nF1 = Capacitor [package=cap-pth-5mm]

nets:
  N1: U1.D25, M1.DI
  N2: U1.D26, M1.RO
  GND: U1.GND, XLR1.1, XLR1.G, XLR2.1, XLR2.G, C1_220uF.+, C2_100nF.1, C3_100nF.1, C4_100nF.2, X1.GND, Squix1.GND, M1.GND, M2.GND, C2_100nF1.2
  VCC: U1.Vin, C1_220uF.-, C2_100nF.2, C3_100nF.2, C4_100nF.1, X1.VBUS, Squix1.VCC, M1.VCC, M2.VCC, C2_100nF1.1
  N3: U1.RX2, M2.RO
  N4: U1.TX2, M2.DI
  N5: U1.D18, M2.RE, M2.DE
  N6: U1.D19, M1.RE, M1.DE
  N7: U1.D21, Squix1.SCA
  N8: U1.D22, Squix1.SCL
  N9: XLR1.2, M1.B
  N10: XLR1.3, M1.A, M1.A1
  N11: XLR2.2, M2.B, M2.B1
  N12: XLR2.3, M2.A, M2.A1

custom parts:
  LuaNode32 / ESP32: New Image for LuaNode32 DOIT ESP32 DEVKIT V1. Base parts from LuaNode32 / ESP32 ESP32 based LuaNode32 by G.Noorlander DOIT Esp32 DevKit v1 (30 pins long, 11 pins width) by Werner Rothschopf (modified by vanepp Dec 2018)
  MAX485 Breakout: MAX485 RS485 breakout board
